// Logisim project rev0.circ as structural Verilog: 2 circuits, main circuit main
module main (
);

  wire demultiplexer_1_out1, demultiplexer_1_out2, demultiplexer_1_out3, demultiplexer_1_out4,
       demultiplexer_1_out5, demultiplexer_1_out6, demultiplexer_1_out7;
  wire [2:0] ram_1_data;
  wire [7:0] adder_1_out, AH_q, AL_q, and_1_out, BL_q, DX_q, not_1_out, or_1_out, ram_1_data_3, ram_2_data,
       register_1_q, S_q, undriven;
  wire [7:3] ram_1_data_2;

  Demultiplexer #(.select(3)) demultiplexer_1 (
    .out1(demultiplexer_1_out1), .out2(demultiplexer_1_out2), .out3(demultiplexer_1_out3),
    .out4(demultiplexer_1_out4), .out5(demultiplexer_1_out5), .out6(demultiplexer_1_out6),
    .out7(demultiplexer_1_out7), .sel(ram_1_data));  // open: out0, in, en
  jump jump_1 (.c(ram_1_data_3), .bus(ram_2_data), .pc(undriven));  // open: reset
  Register register_1 (.D(undriven), .Q(register_1_q), .clk(demultiplexer_1_out1));  // open: en, clr
  Register BL (.D(ram_2_data), .Q(BL_q), .clk(demultiplexer_1_out2));  // open: en, clr
  assign or_1_out = ram_1_data_3 | BL_q;  // OR_Gate or_1, 8 bits wide
  Register AL (.D(ram_2_data), .Q(AL_q), .clk(demultiplexer_1_out3));  // open: en, clr
  Register AH (.D(ram_2_data), .Q(AH_q), .clk(demultiplexer_1_out5));  // open: en, clr
  RAM #(.dataWidth(16)) ram_1 (
    .addr(register_1_q), .data({ram_1_data_3, ram_1_data_2, ram_1_data}));  // open: sel, clk, ld, clr
  Adder adder_1 (.a(or_1_out), .b(AL_q), .out(adder_1_out));  // open: cin, cout
  assign not_1_out = ~AH_q;  // NOT_Gate not_1, 8 bits wide
  assign and_1_out = adder_1_out & not_1_out;  // AND_Gate and_1, 8 bits wide
  Register S (.D(and_1_out), .Q(S_q), .clk(demultiplexer_1_out6));  // open: en, clr
  Register DX (.D(ram_2_data), .Q(DX_q), .clk(demultiplexer_1_out7));  // open: en, clr
  RAM #(.addrWidth(16)) ram_2 (
    .addr({AH_q, adder_1_out}), .data(ram_2_data), .clk(demultiplexer_1_out4));  // open: sel, ld, clr
  assign ram_2_data = S_q ^ DX_q;  // XOR_Gate xor_1, 8 bits wide
endmodule

module jump (
  input  [7:0] c,
  input  reset,
  input  [7:0] bus,
  input  [7:0] pc
);
endmodule
