// Logisim project rev1.circ as structural Verilog: 1 circuit, main circuit main
module main (
);

  wire demultiplexer_1_out1, demultiplexer_1_out3, demultiplexer_2_out0, demultiplexer_2_out1,
       demultiplexer_2_out2, demultiplexer_2_out3, demultiplexer_2_out4, demultiplexer_2_out5,
       demultiplexer_2_out6, nor_2_out, not_1_out, undriven;
  wire [7:0] adder_1_out, ah_q, al_q, and_1_out, bl_q, dx_q, not_2_out, or_1_out, or_2_out, ram_1_data,
       ram_1_data_2, register_1_q, s_q, transistor_1_out, xor_1_out;
  wire [7:7] nor_1_out;
  wire [11:0] counter_1_q;

  Register register_1 (.D(or_1_out), .Q(register_1_q), .clk(demultiplexer_2_out6));  // open: en, clr
  Transistor #(.width(8)) transistor_1 (.in({8{1'b0}}), .out(transistor_1_out), .gate(nor_2_out));
  Demultiplexer #(.select(2)) demultiplexer_1 (
    .out1(demultiplexer_1_out1), .out2(demultiplexer_1_out1), .out3(demultiplexer_1_out3),
    .sel(counter_1_q[11:10]));  // open: out0, in, en
  Counter #(.width(12), .max('hfff)) counter_1 (.Q(counter_1_q), .clk(undriven));  // open: load, D, count, carry, clr
  assign transistor_1_out = nor_2_out ? xor_1_out : 8'bz;  // Controlled_Buffer controlled_buffer_1
  nor nor_1 (nor_1_out[7], xor_1_out[0], xor_1_out[1], xor_1_out[2], xor_1_out[3], xor_1_out[4], xor_1_out[5], xor_1_out[6], xor_1_out[7]);
  nor nor_2 (nor_2_out, ram_1_data_2[0], ram_1_data_2[1], ram_1_data_2[2], ram_1_data_2[3], ram_1_data_2[4], ram_1_data_2[5], ram_1_data_2[6]);
  RAM #(.addrWidth(18), .dataWidth(16)) ram_1 (
    .addr({counter_1_q[9:0], register_1_q}), .data({ram_1_data_2, ram_1_data}), .sel(demultiplexer_1_out1),
    .ld(demultiplexer_1_out1));  // open: clk, clr
  assign or_1_out = transistor_1_out | {nor_1_out[7], ram_1_data_2[6:0]};  // OR_Gate or_1, 8 bits wide
  Demultiplexer #(.select(3)) demultiplexer_2 (
    .out0(demultiplexer_2_out0), .out1(demultiplexer_2_out1), .out2(demultiplexer_2_out2),
    .out3(demultiplexer_2_out3), .out4(demultiplexer_2_out4), .out5(demultiplexer_2_out5),
    .out6(demultiplexer_2_out6), .sel(ram_1_data[2:0]), .en(demultiplexer_1_out3));  // open: out7, in
  not not_1 (not_1_out, ram_1_data[7]);
  Register bl (.D(xor_1_out), .en(ram_1_data[4]), .Q(bl_q), .clk(demultiplexer_2_out5));  // open: clr
  Register al (.D(xor_1_out), .en(ram_1_data[5]), .Q(al_q), .clk(demultiplexer_2_out4));  // open: clr
  Register ah (.D(xor_1_out), .en(ram_1_data[6]), .Q(ah_q), .clk(demultiplexer_2_out3));  // open: clr
  Register s (.D(and_1_out), .en(ram_1_data[7]), .Q(s_q), .clk(demultiplexer_2_out2));  // open: clr
  Register dx (.D(xor_1_out), .en(ram_1_data[3]), .Q(dx_q), .clk(demultiplexer_2_out1));  // open: clr
  assign or_2_out = ram_1_data_2 | bl_q;  // OR_Gate or_2, 8 bits wide
  Adder adder_1 (.a(or_2_out), .b(al_q), .out(adder_1_out));  // open: cin, cout
  assign and_1_out = adder_1_out & not_2_out;  // AND_Gate and_1, 8 bits wide
  assign not_2_out = ~ah_q;  // NOT_Gate not_2, 8 bits wide
  assign xor_1_out = s_q ^ dx_q;  // XOR_Gate xor_1, 8 bits wide
  RAM #(.addrWidth(16)) ram_2 (
    .addr({ah_q, adder_1_out}), .data(xor_1_out), .sel(not_1_out), .clk(demultiplexer_2_out0));  // open: ld, clr
endmodule
