// Logisim project rev2.circ as structural Verilog: 1 circuit, main circuit main
module main (
);

  wire cf_q;
  wire [7:0] adder_1_out, ah_q, al_q, and_1_out, bh_q, bl_q, controlled_buffer_1_out, or_1_out, or_2_out,
       or_3_out, register_1_q, register_2_q, xor_1_out;
  wire [8:8] adder_1_cout;

  D_Flip_Flop cf (.Q(cf_q));  // open: clk, D, Qn, preset, en, reset
  Register al (.Q(al_q));  // open: D, en, clk, clr
  Register bl (.Q(bl_q));  // open: D, en, clk, clr
  Register register_1 (.D(and_1_out), .Q(register_1_q));  // open: en, clk, clr
  Register register_2 (.Q(register_2_q));  // open: D, en, clk, clr
  assign or_1_out = {8{1'b1}} | al_q;  // OR_Gate or_1, 8 bits wide
  assign and_1_out = adder_1_out & ah_q;  // AND_Gate and_1, 8 bits wide
  assign or_2_out = xor_1_out | controlled_buffer_1_out;  // OR_Gate or_2, 8 bits wide
  Adder adder_1 (.a(or_1_out), .b(bl_q), .out(adder_1_out), .cin(cf_q), .cout(adder_1_cout[8]));
  assign xor_1_out = register_1_q ^ register_2_q;  // XOR_Gate xor_1, 8 bits wide
  assign or_3_out = ah_q | bh_q;  // OR_Gate or_3, 8 bits wide
  // Probe on {or_3_out, adder_1_cout[8], adder_1_out}
  assign controlled_buffer_1_out = 1'b0 ? xor_1_out : 8'bz;  // Controlled_Buffer controlled_buffer_1
  Register ah (.Q(ah_q));  // open: D, en, clk, clr
  Register bh (.Q(bh_q));  // open: D, en, clk, clr
  RAM #(.addrWidth(17)) ram_1 (
    .addr({or_3_out, adder_1_cout[8], adder_1_out}), .data(controlled_buffer_1_out), .clk(1'b1), .ld(1'b1));  // open: sel, clr
  // Probe on controlled_buffer_1_out
endmodule
